// Logisim project A1_Group5 circuit.circ as structural Verilog: 3 circuits, main circuit main
module main (
  input  Clear_Everything,
  output [3:0] Opcode,
  output [7:0] out_3,
  output [3:0] out_4,
  output [7:0] out_5,
  output [3:0] out_6,
  output [7:0] PC,
  output [19:0] Read_Address,
  output [3:0] out_9,
  output [7:0] Read_Data_1,
  output [3:0] out_11,
  output [7:0] Read_Data_2,
  output [7:0] Write_Data,
  output [7:0] zero,
  output [7:0] t0,
  output [7:0] t1,
  output [7:0] t2,
  output [7:0] t3,
  output [7:0] t4,
  output [7:0] t5,
  output [7:0] sp
);

  wire alu_8_by_art_1_p4, and_1_out, and_2_out, CLK_out, control_1_alusrc, control_1_beq, control_1_bneq,
       control_1_jump, control_1_memread, control_1_memtoreg, control_1_memwrite, control_1_regdst,
       control_1_regwrite, control_1_shift, not_1_out;
  wire [1:0] priority_encoder_1_out;
  wire [2:0] control_1_aluop;
  wire [3:0] multiplexer_2_out;
  wire [7:0] adder_1_out, adder_2_out, alu_8_by_art_1_p1, alu_8_by_art_1_p2, multiplexer_6_out, ram_1_data;

  Register #(.trigger("falling")) register_1 (
    .D(multiplexer_6_out), .Q(PC), .clk(CLK_out), .clr(Clear_Everything));  // open: en
  Adder adder_1 (.a(PC), .b(8'h1), .out(adder_1_out), .cin(1'b0));  // open: cout
  Clock CLK (.out(CLK_out));
  ROM #(.dataWidth(20)) rom_1 (.addr(PC), .data({Opcode, out_9, out_4, Read_Address[7:4], out_11}));  // open: sel
  Multiplexer #(.width(4), .enable("false")) multiplexer_1 (
    .in0(out_4), .in1(Read_Address[7:4]), .out(out_6), .sel(control_1_regdst));
  Multiplexer #(.width(4), .enable("false")) multiplexer_2 (
    .in0(Read_Address[7:4]), .in1(4'b0000), .out(multiplexer_2_out), .sel(control_1_shift));
  control control_1 (
    .OpCode(Opcode), .ALUOp(control_1_aluop), .ALUSrc(control_1_alusrc), .Bneq(control_1_bneq),
    .Beq(control_1_beq), .MemToReg(control_1_memtoreg), .MemWrite(control_1_memwrite),
    .MemRead(control_1_memread), .RegWrite(control_1_regwrite), .RegDst(control_1_regdst),
    .Shift(control_1_shift), .Jump(control_1_jump));
  register_file register_file_1 (
    .Read_Register_1(out_9), .Read_Register_2(out_4), .Write_Register(out_6), .Write_Data(Write_Data),
    .Write_Signal(control_1_regwrite), .CLK(CLK_out), .Clear(Clear_Everything), .zero(zero), .t0(t0),
    .t1(t1), .t2(t2), .t3(t3), .t4(t4), .t5(t5), .sp(sp), .Read_Data_1(Read_Data_1), .Read_Data_2(Read_Data_2));
  Multiplexer #(.width(8), .enable("false")) multiplexer_3 (
    .in0(Read_Data_2), .in1({multiplexer_2_out, out_11}), .out(out_3), .sel(control_1_alusrc));
  // ALU_8_by_ART alu_8_by_art_1: pin names not known; wires that end beside it: alu_8_by_art_1_p1, alu_8_by_art_1_p2, control_1_aluop, alu_8_by_art_1_p4, out_5
  Multiplexer #(.width(8), .enable("false")) multiplexer_4 (
    .in0(Read_Data_1), .in1(out_3), .out(alu_8_by_art_1_p1), .sel(control_1_shift));
  Adder adder_2 (.a(adder_1_out), .b({multiplexer_2_out, out_11}), .out(adder_2_out));  // open: cin, cout
  Multiplexer #(.width(8), .enable("false")) multiplexer_5 (
    .in0(out_3), .in1(Read_Data_1), .out(alu_8_by_art_1_p2), .sel(control_1_shift));
  and and_1 (and_1_out, control_1_bneq, not_1_out);
  not not_1 (not_1_out, alu_8_by_art_1_p4);
  and and_2 (and_2_out, control_1_beq, alu_8_by_art_1_p4);
  Multiplexer #(.select(2), .width(8), .enable("false")) multiplexer_6 (
    .in0(adder_1_out), .in1(adder_2_out), .in2(adder_2_out), .in3({out_9, out_4}), .out(multiplexer_6_out),
    .sel(priority_encoder_1_out));
  RAM #(.bus("separate")) ram_1 (
    .addr(out_5), .din(Read_Data_2), .data(ram_1_data), .str(control_1_memwrite), .clk(CLK_out),
    .ld(control_1_memread), .clr(Clear_Everything));  // open: sel
  Priority_Encoder #(.select(2)) priority_encoder_1 (
    .in0(1'b1), .in1(and_1_out), .in2(and_2_out), .in3(control_1_jump), .out(priority_encoder_1_out));  // open: gs, en_out, en_in
  Multiplexer #(.width(8), .enable("false")) multiplexer_7 (
    .in0(out_5), .in1(ram_1_data), .out(Write_Data), .sel(control_1_memtoreg));

  assign {Read_Address[19:8], Read_Address[3:0]} = {Opcode, out_9, out_4, out_11};

  // Notes on the sheet:
  //   Clear CLK
  //   contents of rom_1 (hex, n*v repeats v):
  //   d010a d0201 e1209 d0202 e1209 d0201 d0301 d0502 42340 40320 40430 d5501 251fb c0f00 d0401 37400
  //   a7701 84014 37100 a7701 61055 37500 a7701 355a2 37500 a7701 952a2 37200 a7701 d2388 37300 a7701
  //   a3481 f4340 37400 a7701 d0146 d0255 71230 37300 a7701 534fe 37400 a7701 d0480 d05aa 14520 37200
  //   a7701 b23ff 37300 a7701 c3400
  //   Clear Register
  //   Data Memory
  //   Clear Memory
endmodule

// Register File
module register_file (
  input  [3:0] Read_Register_1,
  input  [3:0] Read_Register_2,
  input  [3:0] Write_Register,
  input  [7:0] Write_Data,
  input  Write_Signal,
  input  CLK,
  input  Clear,
  output [7:0] Read_Data_1,
  output [7:0] Read_Data_2,
  output [7:0] sp,
  output [7:0] zero,
  output [7:0] t5,
  output [7:0] t0,
  output [7:0] t4,
  output [7:0] t1,
  output [7:0] t2,
  output [7:0] t3
);

  wire and_1_out, and_2_out, and_3_out, and_4_out, and_5_out, and_6_out, and_7_out, and_8_out,
       decoder_1_out0, decoder_1_out1, decoder_1_out2, decoder_1_out3, decoder_1_out4, decoder_1_out5,
       decoder_1_out6, decoder_1_out7, multiplexer_1_out, multiplexer_3_out;
  wire [7:0] multiplexer_2_out;

  Decoder #(.select(4), .enable("false")) decoder_1 (
    .out0(decoder_1_out0), .out1(decoder_1_out1), .out2(decoder_1_out2), .out3(decoder_1_out3),
    .out4(decoder_1_out4), .out5(decoder_1_out5), .out6(decoder_1_out6), .out7(decoder_1_out7),
    .sel(Write_Register));  // open: out8, out9, out10, out11, out12, out13, out14, out15
  and and_1 (and_1_out, decoder_1_out0, 1'b0);
  and and_2 (and_2_out, decoder_1_out1, Write_Signal);
  and and_3 (and_3_out, decoder_1_out2, Write_Signal);
  and and_4 (and_4_out, decoder_1_out3, Write_Signal);
  and and_5 (and_5_out, decoder_1_out4, Write_Signal);
  and and_6 (and_6_out, decoder_1_out5, Write_Signal);
  and and_7 (and_7_out, decoder_1_out6, Write_Signal);
  and and_8 (and_8_out, decoder_1_out7, Write_Signal);
  Multiplexer #(.enable("false")) multiplexer_1 (.in0(and_8_out), .in1(Clear), .out(multiplexer_1_out), .sel(Clear));
  Multiplexer #(.width(8), .enable("false")) multiplexer_2 (
    .in0(Write_Data), .in1({8{1'b1}}), .out(multiplexer_2_out), .sel(Clear));
  Register u_zero (.D(Write_Data), .en(and_1_out), .Q(zero), .clk(CLK), .clr(Clear));
  Register u_t0 (.D(Write_Data), .en(and_2_out), .Q(t0), .clk(CLK), .clr(Clear));
  Register u_t1 (.D(Write_Data), .en(and_3_out), .Q(t1), .clk(CLK), .clr(Clear));
  Register u_t2 (.D(Write_Data), .en(and_4_out), .Q(t2), .clk(CLK), .clr(Clear));
  Register u_t3 (.D(Write_Data), .en(and_5_out), .Q(t3), .clk(CLK), .clr(Clear));
  Register u_t4 (.D(Write_Data), .en(and_6_out), .Q(t4), .clk(CLK), .clr(Clear));
  Register u_t5 (.D(Write_Data), .en(and_7_out), .Q(t5), .clk(CLK), .clr(Clear));
  Register u_sp (.D(multiplexer_2_out), .en(multiplexer_1_out), .Q(sp), .clk(multiplexer_3_out));  // open: clr
  Multiplexer #(.enable("false")) multiplexer_3 (.in0(CLK), .in1(Clear), .out(multiplexer_3_out), .sel(Clear));
  Multiplexer #(.select(4), .width(8), .enable("false")) multiplexer_4 (
    .in0(zero), .in1(t0), .in2(t1), .in3(t2), .in4(t3), .in5(t4), .in6(t5), .in7(sp), .out(Read_Data_1),
    .sel(Read_Register_1));  // open: in8, in9, in10, in11, in12, in13, in14, in15
  Multiplexer #(.select(4), .width(8), .enable("false")) multiplexer_5 (
    .in0(zero), .in1(t0), .in2(t1), .in3(t2), .in4(t3), .in5(t4), .in6(t5), .in7(sp), .out(Read_Data_2),
    .sel(Read_Register_2));  // open: in8, in9, in10, in11, in12, in13, in14, in15
endmodule

// Control
module control (
  input  [3:0] OpCode,
  output [2:0] ALUOp,
  output ALUSrc,
  output Bneq,
  output Beq,
  output MemToReg,
  output MemWrite,
  output MemRead,
  output RegWrite,
  output RegDst,
  output Shift,
  output Jump
);

  ROM #(.addrWidth(4), .dataWidth(13)) rom_1 (
    .addr(OpCode),
    .data({Jump, Shift, RegDst, RegWrite, MemRead, MemWrite, MemToReg, Beq, Bneq, ALUSrc, ALUOp}));  // open: sel

  // Notes on the sheet:
  //   contents of rom_1 (hex, n*v repeats v):
  //   604 602 11 88 600 20b e0d 603 e0e 348 209 20a 1000 208 21 601
endmodule
